# Fritzing sketch ALT-UNO (saved by Fritzing 0.9.10b)
breadboards: 1

parts:
  Arduino_Nano = Arduino Nano (Rev3.0)
  BUZZER = Piezo Speaker
  S1 = Pushbutton [package="[THT]"]
  R1 = Resistor [tolerance=±5% power=0.25 resistance=10k package=THT]
  LCD1 = 20x4 LCD display [part_number=2004A]
  M1 = JSN-SRO4T [package=THT]

nets:
  GND: Arduino_Nano.GND, BUZZER.pin1, S1.Pin_2, LCD1.Vss, M1.pin1
  N1: Arduino_Nano.D2, M1.pin3
  N2: Arduino_Nano.D3, S1.Pin_3, R1.Pin_0
  N3: Arduino_Nano.D4, BUZZER.pin2
  N4: Arduino_Nano.D5, M1.pin2
  N5: Arduino_Nano.D6, LCD1.DB7
  N6: Arduino_Nano.D7, LCD1.DB6
  N7: Arduino_Nano.D8, LCD1.DB5
  N8: Arduino_Nano.D9, LCD1.DB4
  N9: Arduino_Nano.D10, LCD1.E
  N10: Arduino_Nano.D11/MOSI, LCD1.RS
  N11: Arduino_Nano.D12/MISO, LCD1.A_+
  5V: Arduino_Nano.5V, R1.Pin_1, LCD1.Vdd, M1.pin4

custom parts:
  20x4 LCD display: 20x4 character display. CHECK LED POLARITY BEFORE CONNECTING POWER Some versions of the dispaly have the polarity of the LED pins "A" and "K" reversed.
  JSN-SRO4T: JSN-SR04T Waterproof Ultrasonic Distance Measuring Module Integrated Ultrasonic Detection Module DC 5V.
